# Fritzing sketch start (saved by Fritzing 0.9.6b)
breadboards: 1

parts:
  Part1 = Arduino Uno (Rev3) - ICSP
  HC-1 = HC-12 Module
  R1 = Trimmer Potentiometer [maximum_resistance=10kΩ package=THT]

nets:
  N1: Part1.A0, R1.wiper
  GND: Part1.GND, HC-1.GND, R1.leg1
  N2: Part1.D8, HC-1.RXD
  N3: Part1.D9_PWM, HC-1.TXD
  5V: Part1.5V, HC-1.VCC, R1.leg2

custom parts:
  HC-12 Module: HC-12 433Mhz Module
